// Logisim project AND_Gate.circ as structural Verilog: 2 circuits, main circuit main
module main (
  input  A,
  input  B,
  output Y
);

  and and_1 (Y, B, A);
endmodule

// A
module AND_Gate (
  input  A,
  input  B,
  output Y
);

  and and_1 (Y, B, A);
endmodule
