// Logisim project AND_GATE.circ as structural Verilog: 2 circuits, main circuit main
module main (
);

  wire undriven, undriven_2;

  // AND_Gate and_1 has open pins: in0=undriven, in1=undriven_2, out=open
endmodule

module Add_Gate (
  input  in_1,
  input  in_2,
  output out_3
);

  and and_1 (out_3, in_1, in_2);
endmodule
