// Logisim project XOR_Gate.circ as structural Verilog
module XOR_Gate (
  input  in_1,
  input  in_2,
  output out_3
);

  xor xor_1 (out_3, in_1, in_2);
endmodule
